# Fritzing sketch Schematic (saved by Fritzing 0.9.3b)
breadboards: 1

parts:
  Part1 = Arduino Mega 2560 (Rev3)
  LED1 = LED - 5mm [color="Red (633nm)" package="5 mm [THT]"]
  LED2 = LED - 5mm [color="Green (560nm)" package="5 mm [THT]"]
  LED3 = LED - 5mm [color="Blue (505nm)" package="5 mm [THT]"]
  R1 = Rotary Potentiometer (Small) [maximum_resistance=100kΩ package=THT]
  R2 = Rotary Potentiometer (Small) [maximum_resistance=100kΩ package=THT]
  S1 = Pushbutton [package="[THT]"]
  S2 = Pushbutton [package="[THT]"]
  R3 = Resistor [tolerance=±5% resistance=220 package=THT]
  R4 = Resistor [tolerance=±5% resistance=220 package=THT]
  R5 = Resistor [tolerance=±5% resistance=220 package=THT]
  S3 = Toggle Switch [package=THT]
  S4 = Toggle Switch [package=THT]

nets:
  N1: Part1.A0, R1.wiper
  N2: Part1.A1, R2.wiper
  N3: Part1.D19/RX1, S3.COM
  N4: Part1.D18/TX1, S4.COM
  N5: Part1.D12_PWM, R5.Pin_0
  N6: Part1.D11_PWM, R4.Pin_0
  N7: Part1.D10_PWM, R3.Pin_0
  N8: Part1.D2_PWM, S2.Pin_1, S2.Pin_2
  N9: Part1.D3_PWM, LED1.anode, LED2.anode, LED3.anode, R1.leg2, R2.leg2, S1.Pin_1, S1.Pin_2, S3.L2, S4.L2
  N10: LED1.cathode, R3.Pin_1
  N11: LED2.cathode, R4.Pin_1
  N12: LED3.cathode, R5.Pin_1
  N13: R1.leg1, R2.leg1, S1.Pin_3, S1.Pin_4, S2.Pin_3, S2.Pin_4, S3.L1, S4.L1
