# Fritzing sketch HBridge (saved by Fritzing 0.9.3b)
breadboards: 1

parts:
  IC1 = H-Bridge [package=THT]
  C1 = Capacitor [package=0805]
  C1_2 = Capacitor [package=cap-pth-5mm]
  C1_3 = Capacitor [package=cap-pth-large]
  C2 = Capacitor [package=cap-pth-5mm]  # not connected
  C3 = Capacitor [package=cap-pth-large]  # not connected
  C4 = Capacitor [package=0805]
  M1 = DC Motor
  M2 = DC Motor
  Part1 = Arduino Mega 2560 (Rev3)

nets:
  5V: IC1.1_2EN, IC1.VCC2, IC1.3_4EN
  N1: IC1.1A, Part1.D11_PWM
  N2: IC1.1Y, C1.1, C1_2.1, C1_3.1, M2.pin_1
  GND: IC1.GND1, IC1.GND2, IC1.GND3, IC1.GND4
  N3: IC1.2Y, C1.2, C1_2.2, C1_3.2, M2.pin_2
  N4: IC1.2A, Part1.D9_PWM
  N5: IC1.3A, Part1.D12_PWM
  N6: IC1.3Y, C4.2, M1.pin_2
  N7: IC1.4Y, C4.1, M1.pin_1
  N8: IC1.4A, Part1.D10_PWM
  9V: IC1.VCC1
