# Fritzing sketch Color Sensor (saved by Fritzing 0.9.3b)
breadboards: 1

parts:
  Part1 = Arduino Mega 2560 (Rev3)
  R1 = Resistor [tolerance=±5% resistance=120 package=THT]
  R2 = Resistor [tolerance=±5% resistance=51 package=THT]
  Q1 = LTR-301 [package=ltr-301]
  R3 = Resistor [tolerance=±5% resistance=220 package=THT]
  LED2 = LED - 5mm [color="Blue (505nm)" package="5 mm [THT]"]
  LED1 = LED - 5mm [color="Red (633nm)" package="5 mm [THT]"]

nets:
  N1: Part1.A0, Q1.E, R3.Pin_0
  N2: Part1.D51, LED2.anode
  N3: Part1.D53, LED1.anode
  N4: R1.Pin_0, LED1.cathode
  GND: R1.Pin_1, R2.Pin_1, R3.Pin_1
  N5: R2.Pin_0, LED2.cathode
  5V: Q1.C
