# Fritzing sketch Hall Sensor (saved by Fritzing 0.9.3b)
breadboards: 1

parts:
  Hall_Effect_(Wrong_Part_Number) = HALL-EFFECT [package=sc70]
  LED1 = LED - 5mm [color="Red (633nm)" package="5 mm [THT]"]
  R1 = Resistor [tolerance=±5% resistance=220 package=THT]

nets:
  GND: Hall_Effect_(Wrong_Part_Number).GND
  5V: Hall_Effect_(Wrong_Part_Number).VCC, R1.Pin_0
  N1: Hall_Effect_(Wrong_Part_Number).OUT, LED1.cathode
  N2: LED1.anode, R1.Pin_1
