# Fritzing sketch collision_detection (saved by Fritzing 0.9.3b)
stripboards: 1

parts:
  R1 = Resistor [tolerance=±5% resistance=220 package="1206 [SMD]"]
  LED1 = LED - 5mm [color="Yellow (592nm)" package="5 mm [THT]"]
  7_Segment1 = 7 Segment Display
  R2 = Resistor [tolerance=±5% resistance=220 package=THT]
  R3 = Resistor [tolerance=±5% resistance=220 package=THT]
  R4 = Resistor [tolerance=±5% resistance=220 package=THT]
  R5 = Resistor [tolerance=±5% resistance=220 package=THT]
  R6 = Resistor [tolerance=±5% resistance=220 package=THT]
  R7 = Resistor [tolerance=±5% resistance=220 package=THT]
  R8 = Resistor [tolerance=±5% resistance=220 package=THT]
  LED2 = LED - 5mm [color="Red (633nm)" package="5 mm [THT]"]
  LED3 = LED - 5mm [color="Green (555nm)" package="5 mm [THT]"]
  LED4 = LED - 5mm [color="Blue (470nm)" package="5 mm [THT]"]
  R9 = Resistor [tolerance=±5% resistance=220 package=THT]
  R10 = Resistor [tolerance=±5% resistance=220 package=THT]
  R11 = Resistor [tolerance=±5% resistance=220 package=THT]
  D2F1 = D2F-FL Omron Snap Action Limit Switch with Level
  D2F2 = D2F-FL Omron Snap Action Limit Switch with Level
  Q1 = LTR-301 [package=ltr-301]
  R12 = Resistor [tolerance=±5% resistance=220 package=THT]

nets:
  N1: R1.Pin_1, LED1.cathode
  N2: LED1.anode, D2F1.COM, D2F2.COM, Q1.E
  N3: 7_Segment1.Segment_G, R3.Pin_1
  N4: 7_Segment1.Segment_F, R2.Pin_1
  N5: 7_Segment1.common_anode, 7_Segment1.Segment_C, LED2.anode, LED3.anode, LED4.anode, D2F1.NC, D2F2.NC, R12.Pin_0
  N6: 7_Segment1.Segment_E, R4.Pin_1
  N7: 7_Segment1.Segment_D, R5.Pin_1
  N8: 7_Segment1.Segment_DP, R6.Pin_0
  N9: 7_Segment1.Segment_B, R8.Pin_0
  N10: 7_Segment1.Segment_A, R7.Pin_0
  N11: LED2.cathode, R9.Pin_1
  N12: LED3.cathode, R10.Pin_1
  N13: LED4.cathode, R11.Pin_1

notes:
  V+ = +5V
  Horn?

custom parts:
  D2F-FL Omron Snap Action Limit Switch with Level: Snap action switch with stainless steel lever.
