# Fritzing sketch headlights (saved by Fritzing 0.9.3b)
stripboards: 1

parts:
  LED1 = LED - 5mm [color="White (8000K)" package="5 mm [THT]"]
  LED2 = LED - 5mm [color="White (8000K)" package="5 mm [THT]"]
  R2 = Resistor Mini [tolerance=±5% resistance=51 package=THT]
  R3 = Resistor Mini [tolerance=±5% resistance=51 package=THT]
  LED3 = LED - 5mm [color="Yellow (595nm)" package="5 mm [THT]"]
  LED4 = LED - 5mm [color="Yellow (595nm)" package="5 mm [THT]"]
  R4 = Resistor Mini [tolerance=±5% resistance=220 package=THT]
  R5 = Resistor Mini [tolerance=±5% resistance=220 package=THT]
  LED5 = LED - 5mm [color="Red (635nm)" package="5 mm [THT]"]
  LED6 = LED - 5mm [color="Red (635nm)" package="5 mm [THT]"]
  R6 = Resistor Mini [tolerance=±5% resistance=220 package=THT]
  R7 = Resistor Mini [tolerance=±5% resistance=220 package=THT]

nets:
  N1: LED1.cathode, R3.Pin_1
  N2: LED2.cathode, R2.Pin_1
  N3: LED3.cathode, R5.Pin_0
  N4: LED4.cathode, R4.Pin_0
  N5: R4.Pin_1, R7.Pin_1
  N6: R5.Pin_1, R6.Pin_1
  N7: LED5.cathode, R7.Pin_0
  N8: LED6.cathode, R6.Pin_0

custom parts:
  Resistor Mini: A generic resistor (0.25W)
