# Fritzing sketch receiver (saved by Fritzing 0.9.3b)
stripboards: 1

parts:
  LM1 = LM741 [part_number=LM741 package="DIP (Dual Inline) [THT]"]
  LM3 = LM741 [part_number=LM741 package="DIP (Dual Inline) [THT]"]
  LM2 = LM741 [part_number=LM741 package="DIP (Dual Inline) [THT]"]
  C4 = Ceramic Capacitor [capacitance=100nF package="200 mil [THT, multilayer]"]
  C6 = Ceramic Capacitor [capacitance=100nF package="200 mil [THT, multilayer]"]
  C7 = Ceramic Capacitor [capacitance=100nF package="200 mil [THT, multilayer]"]
  C8 = Ceramic Capacitor [capacitance=100nF package="200 mil [THT, multilayer]"]
  C9 = Ceramic Capacitor [capacitance=100nF package="200 mil [THT, multilayer]"]
  MIC1 = Microphone
  D1 = P1000K [part_number=P1000K]
  R9 = Resistor Mini [tolerance=±5% resistance=220 package=THT]
  R10 = Resistor Mini [tolerance=±5% resistance=220 package=THT]
  R11 = Resistor Mini [tolerance=±5% resistance=220 package=THT]
  R12 = Resistor Mini [tolerance=±5% resistance=220 package=THT]
  R13 = Resistor Mini [tolerance=±5% resistance=220 package=THT]
  R14 = Resistor Mini [tolerance=±5% resistance=220 package=THT]
  R15 = Resistor Mini [tolerance=±5% resistance=220 package=THT]
  R16 = Resistor Mini [tolerance=±5% resistance=220 package=THT]

nets:
  N1: LM1.pin2, C8.1, R12.Pin_0
  N2: LM1.pin6, R12.Pin_1
  N3: LM1.pin7, LM3.pin7, LM2.pin7
  N4: LM3.pin2, R14.Pin_1, R16.Pin_1
  N5: LM3.pin6, D1.anode, R14.Pin_0
  N6: LM2.pin2, C9.1, R15.Pin_1
  N7: LM2.pin6, C6.0, C7.1, R15.Pin_0
  N8: C4.0, MIC1.pin1, R9.Pin_1, R10.Pin_1, R13.Pin_1
  N9: C4.1, D1.cathode, R13.Pin_0
  N10: C6.1, C9.0, R10.Pin_0, R11.Pin_1
  N11: C7.0, R16.Pin_0
  N12: C8.0, MIC1.pin2, R9.Pin_0

custom parts:
  LM741: This is a single Op Amp DIP.
  Resistor Mini: A generic resistor (0.25W)
