# Fritzing sketch sensor_board (saved by Fritzing 0.9.3b)
stripboards: 1

parts:
  U1 = HALL-EFFECT [package=sc70]
  R1 = Resistor [tolerance=±5% resistance=1k package="0402 [SMD]"]
  R2 = Resistor [tolerance=±5% resistance=220 package="1206 [SMD]"]
  LED1 = LED - 5mm [color="Blue (470nm)" package="5 mm [THT]"]
  R3 = Resistor [tolerance=±5% resistance=510 package="1206 [SMD]"]
  LED2 = LED - 5mm [color="Red (633nm)" package="5 mm [THT]"]
  P1 = S1133 Si Photodiode [package="8mm Ceramic [THT]"]
  R4 = Resistor [tolerance=±5% resistance=130 package="0402 [SMD]"]

nets:
  N1: U1.GND, R1.Pin_1, P1.anode
  N2: U1.VCC, LED1.anode, LED2.cathode
  N3: U1.OUT, R1.Pin_0
  N4: R2.Pin_1, P1.cathode
  N5: LED1.cathode, R3.Pin_1
  N6: LED2.anode, R4.Pin_0
