# Fritzing sketch transmitter (saved by Fritzing 0.9.3b)
stripboards: 1

parts:
  U1 = SN74LS32N [package="DIP14 [THT]"]
  LM1 = LM741 [part_number=LM741 package="DIP (Dual Inline) [THT]"]
  Q1 = TRANSISTOR_NPN [package=to-92]
  Q2 = PNP-Transistor [package="TO92 [THT]"]
  SP1 = SPEAKER [package=pcb_mount_speaker]
  SP2 = SPEAKER [package=pcb_mount_speaker]
  C1 = Ceramic Capacitor [capacitance="100 nF" package="0603 [SMD, multilayer]"]

nets:
  N1: U1.1Y, LM1.pin3
  N2: U1.GND, Q2.E, SP1.+, SP2.+
  N3: U1.Vcc, LM1.pin7, Q1.C
  N4: LM1.pin2, LM1.pin6, Q1.B, Q2.B
  N5: Q1.E, Q2.C, C1.0
  N6: SP1.-, SP2.-, C1.1

custom parts:
  LM741: This is a single Op Amp DIP.
