# Fritzing sketch voltage_regulator_and_hbridge (saved by Fritzing 0.9.3b)
stripboards: 1

parts:
  IC1 = Voltage Regulator [package=to-220-alt]
  IC2 = Voltage Regulator [package=to-220-alt]
  C1 = Ceramic Capacitor [capacitance="100 nF" package="1206 [SMD, multilayer]"]
  C2 = Ceramic Capacitor [capacitance="100 nF" package="1206 [SMD, multilayer]"]
  C3 = Ceramic Capacitor [capacitance="100 nF" package="1206 [SMD, multilayer]"]
  C4 = Ceramic Capacitor [capacitance="100 nF" package="1206 [SMD, multilayer]"]
  LM1 = LM741 [part_number=LM741 package="DIP (Dual Inline) [THT]"]
  R1 = Resistor Mini [tolerance=±5% resistance=220 package=THT]
  C5 = Ceramic Capacitor [capacitance="100 nF" package="1206 [SMD, multilayer]"]
  IC3 = H-Bridge [package=THT]
  D2F1 = D2F-FL Omron Snap Action Limit Switch with Level

nets:
  N1: IC1.GND, C3.0
  GND1: IC1.IN, IC2.IN, C1.1, C2.0, C3.1, C4.0, LM1.pin3, IC3.GND1, IC3.GND2, IC3.GND3, IC3.GND4, D2F1.NC
  N2: IC1.OUT, C1.0
  N3: IC2.GND, C2.1
  N4: IC2.OUT, C4.1, C5.0
  N5: LM1.pin2, R1.Pin_1, C5.1
  N6: LM1.pin6, R1.Pin_0
  N7: IC3.1_2EN, IC3.3_4EN, IC3.VCC1, D2F1.COM

notes:
  -9V
  9V
  +V = 5V

custom parts:
  LM741: This is a single Op Amp DIP.
  Resistor Mini: A generic resistor (0.25W)
  D2F-FL Omron Snap Action Limit Switch with Level: Snap action switch with stainless steel lever.
